# Fritzing sketch SDS011_LCD_WIFI (saved by Fritzing 0.8.7b)
circuit board: 8.46667cm x 5.64444cm

parts:
  LCM1602_IIC1 = LCM1602 IIC [part_number="LCM1602 IIC" chip_label="LCM1602 IIC" package="DIP (Dual Inline) [THT]"]
  LCD1 = LCD screen
  WeMos_D1_Mini_Battery_Shield1 = WeMos D1 Mini Battery Shield
  WeMos_D1_Mini1 = WeMos D1 Mini
  SDS1 = SDS011 - dust sensor [part_number=1]
  AO3401A = Basic FET P-Channel [package="TO220 [THT]"]
  BAT1 = Battery Holders [package=lipo-1100mAh]
  R1 = Resistor [tolerance=±5% resistance=10k package=THT]
  D1 = Diode [package=diode-1n4148]
  D2 = Diode [package=diode-1n4148]
  D3 = Diode [package=diode-1n4148]
  Display = Round Pushbutton
  Continious_1_sec = Round Pushbutton
  WI-FI = Round Pushbutton
  ON_-_OFF = Round Pushbutton
  R3 = Resistor [tolerance=±5% resistance=44k package=THT]
  R4 = Resistor [tolerance=±5% resistance=51k package=THT]  # not connected

nets:
  VSS: LCM1602_IIC1.VSS, LCD1.VSS
  VDD: LCM1602_IIC1.VDD, LCD1.VDD
  N1: LCM1602_IIC1.V0, LCD1.V0
  N2: LCM1602_IIC1.RS, LCD1.RS
  N3: LCM1602_IIC1.RW, LCD1.R/W
  N4: LCM1602_IIC1.E, LCD1.E
  N5: LCM1602_IIC1.D0, LCD1.DB0
  N6: LCM1602_IIC1.D1, LCD1.DB1
  N7: LCM1602_IIC1.D2, LCD1.DB2
  N8: LCM1602_IIC1.D3, LCD1.DB3
  N9: LCM1602_IIC1.D4, LCD1.DB4
  N10: LCM1602_IIC1.D5, LCD1.DB5
  N11: LCM1602_IIC1.D6, LCD1.DB6
  N12: LCM1602_IIC1.D7, LCD1.DB7
  N13: LCM1602_IIC1.A, LCD1.LED+
  N14: LCM1602_IIC1.K, LCD1.LED-
  GND: LCM1602_IIC1.GND, WeMos_D1_Mini1.G, SDS1.GND, Continious_1_sec.leg1, WI-FI.leg0
  N15: LCM1602_IIC1.VCC, Display.leg1, R3.Pin_1
  N16: LCM1602_IIC1.SDA, WeMos_D1_Mini1.D3
  N17: LCM1602_IIC1.SCL, WeMos_D1_Mini1.D4
  N18: LCM1602_IIC1.LED_A, LCM1602_IIC1.LED_B
  N19: WeMos_D1_Mini_Battery_Shield1.5V, AO3401A.source
  N20: WeMos_D1_Mini1.D0, WeMos_D1_Mini1.RST
  N21: WeMos_D1_Mini1.D1, SDS1.RX
  N22: WeMos_D1_Mini1.D2, SDS1.TX
  N23: WeMos_D1_Mini1.D7, WI-FI.leg1
  N24: WeMos_D1_Mini1.RX, Continious_1_sec.leg0
  N25: AO3401A.gate, R1.Pin_0, D3.C
  N26: AO3401A.drain, Display.leg0
  N27: BAT1.+, ON_-_OFF.leg0
  N28: D1.C, D2.A
  N29: D2.C, D3.A

custom parts:
  LCM1602 IIC: I2C-Module to use a 1602 or 2004 LCD on with the wire.h libory Serial LCD Modul
  WeMos D1 Mini: The D1 mini is a mini wifi board based on ESP-8266EX.
  SDS011 - dust sensor: The SDS 011 Sensor is a quite recent Air Quality Sensor developed by inovafit, a spin-off from the university of Jinan (in Shandong). With its size, it is probably one of the best sensor in terms of accuracy: While other sensors tend to focus on shrinking the sensor size, the SDS 011 has opted for a size tradeoff allowing it to use a larger fan. And the larger the fan, the better the quality.

// code stored in the sketch: AnalogReadSerial2LCD_LED.ino
#include <Wire.h>
#include <LiquidCrystal_I2C.h>

LiquidCrystal_I2C lcd(0x27, 16, 2);   // adress and format LCD

const int analogInPin = A0;           // Analog input pin that the potentiometer is attached to
const int analogOutPin = 9;           // Analog output pin that the LED is attached to

int sensorValue = 0;                  // value read from the pot
int outputValue = 0;                  // value output to the PWM (analog out)

void setup() {
  lcd.init();                         // init LCD
  lcd.backlight();
  lcd.home();
  lcd.setCursor(5, 0);                // place static text
  lcd.print("ADC = ");
  lcd.setCursor(15, 0);
  lcd.print("V");
  lcd.setCursor(0, 1);
  lcd.print("LED : ");
  lcd.setCursor(12, 1);
  lcd.print("%");
  Serial.begin(9600);                 // optional serial monitor
}

void loop() {
  int sensorValue = analogRead(analogInPin);          // read analog A0 en store in sensorValue
  float voltValue = 5.0 / 1024.0 * sensorValue;       // calculate volt at analog A0 and store in voltValue
  float percentValue = sensorValue / 1024.0 * 100.0;  // calculate percentage analog A0 and store in percentValue
  outputValue = map(sensorValue, 0, 1023, 0, 255);    // map analog input to analog output and store in outputValue
  analogWrite(analogOutPin, outputValue);             // write outputValue to analogOutPin

  lcd.setCursor(0, 0);                                // set cursor at deserid position
  leadingZeros(sensorValue, 4);                       // print sensorvalue with number of leading-characters (0 or space as specified in function leadingZeros)
  lcd.setCursor(10, 0);                               // set cursor at deserid position
  lcd.print(voltValue);                               // print voltValue
  lcd.setCursor(6, 1);                                // set cursor at deserid position
  lcd.print(percentValue);                            // print percentValue

  Serial.print("sensor = " );                         // print the results to the serial monitor:
  Serial.print(sensorValue);
  Serial.print("\t output = ");
  Serial.print(outputValue);
  Serial.print("\t procent = ");
  Serial.println(percentValue);

  delay(1000);                                        // set delay
}

void leadingZeros( int value, int width) {            // display result with leading characters
  char valueStr[6];                                   // large enough to hold an int
  itoa (value, valueStr, 10);                         // itoa converts int to string
  int len = strlen(valueStr);                         // calculate length of valueStr
  if (len < width) {
    len = width - len;
    while (len--)
      lcd.print(' ');                                 // for leading zeros place '0' between (), for leading spaces place ' ' between ()
  }
  lcd.print(valueStr);
}
